// Logisim project Lucas_de_Souza_Cerveira_Pereira.circ as structural Verilog: 12 circuits, main circuit main
module somador_1bit (
  input  c_in,
  input  a,
  input  b,
  output out_4,
  output out_5
);

  wire and_1_out, and_2_out, and_3_out, xor_1_out;

  xor xor_1 (xor_1_out, a, b);
  xor xor_2 (out_4, xor_1_out, c_in);
  and and_1 (and_1_out, a, c_in);
  and and_2 (and_2_out, a, b);
  and and_3 (and_3_out, b, c_in);
  or or_1 (out_5, and_1_out, and_2_out, and_3_out);
endmodule

module main (
  input  in_1,
  input  in_2,
  input  in_3,
  input  in_4,
  input  in_5,
  input  in_6,
  input  in_7,
  input  in_8,
  input  in_9,
  input  in_10,
  input  [2:0] in_11,
  input  in_12,
  input  in_13,
  input  in_14,
  input  in_15,
  output carry,
  output a_maior_b,
  output a_igual_b,
  output zero
);

  wire or_1_out;
  wire [7:0] ACC_q, controlled_buffer_1_out, MAR_q, R0_q, R1_q, R2_q, R3_q, TMP_q, ula_1_out_5;

  ula ula_1 (
    .in_2(controlled_buffer_1_out), .in_3(TMP_q), .out_5(ula_1_out_5), .in_1(in_11), .out_4(carry),
    .a_maior_que_b(a_maior_b), .a_igual_b(a_igual_b), .out_8(zero));
  Register TMP (.D(controlled_buffer_1_out), .Q(TMP_q), .clk(in_2));  // open: en, clr
  Register ACC (.D(ula_1_out_5), .Q(ACC_q), .clk(in_14));  // open: en, clr
  assign controlled_buffer_1_out = in_15 ? ACC_q : 8'bz;  // Controlled_Buffer controlled_buffer_1
  Register R0 (.D(controlled_buffer_1_out), .Q(R0_q), .clk(in_5));  // open: en, clr
  assign controlled_buffer_1_out = in_6 ? R0_q : 8'bz;  // Controlled_Buffer controlled_buffer_2
  Register R1 (.D(controlled_buffer_1_out), .Q(R1_q), .clk(in_7));  // open: en, clr
  assign controlled_buffer_1_out = in_8 ? R1_q : 8'bz;  // Controlled_Buffer controlled_buffer_3
  assign controlled_buffer_1_out = in_10 ? R2_q : 8'bz;  // Controlled_Buffer controlled_buffer_4
  Register R2 (.D(controlled_buffer_1_out), .Q(R2_q), .clk(in_9));  // open: en, clr
  // Probe on controlled_buffer_1_out
  Register R3 (.D(controlled_buffer_1_out), .Q(R3_q), .clk(in_3));  // open: en, clr
  assign controlled_buffer_1_out = in_4 ? R3_q : 8'bz;  // Controlled_Buffer controlled_buffer_5
  Register MAR (.D(controlled_buffer_1_out), .Q(MAR_q), .clk(in_1));  // open: en, clr
  or or_1 (or_1_out, in_12, in_13);
  RAM #(.databus("bidir")) ram_1 (.addr(MAR_q), .we(in_12), .oe(in_13), .clk(or_1_out));  // open: data

  // Notes on the sheet:
  //   Lucas de Souza Cerveira Pereira - 22401904
endmodule

module somador_8bit (
  input  in_1,
  input  [7:0] in_2,
  input  [7:0] in_3,
  output [7:0] out_4,
  output out_5
);

  wire somador_1bit_1_out_5, somador_1bit_2_out_5, somador_1bit_3_out_5, somador_1bit_4_out_5,
       somador_1bit_5_out_5, somador_1bit_6_out_5, somador_1bit_7_out_5;

  somador_1bit somador_1bit_1 (.a(in_2[0]), .b(in_3[0]), .c_in(in_1), .out_4(out_4[0]), .out_5(somador_1bit_1_out_5));
  somador_1bit somador_1bit_2 (
    .a(in_2[1]), .b(in_3[1]), .c_in(somador_1bit_1_out_5), .out_4(out_4[1]), .out_5(somador_1bit_2_out_5));
  somador_1bit somador_1bit_3 (
    .a(in_2[2]), .b(in_3[2]), .c_in(somador_1bit_2_out_5), .out_4(out_4[2]), .out_5(somador_1bit_3_out_5));
  somador_1bit somador_1bit_4 (
    .a(in_2[3]), .b(in_3[3]), .c_in(somador_1bit_3_out_5), .out_4(out_4[3]), .out_5(somador_1bit_4_out_5));
  somador_1bit somador_1bit_5 (
    .a(in_2[4]), .b(in_3[4]), .c_in(somador_1bit_4_out_5), .out_4(out_4[4]), .out_5(somador_1bit_5_out_5));
  somador_1bit somador_1bit_6 (
    .a(in_2[5]), .b(in_3[5]), .c_in(somador_1bit_5_out_5), .out_4(out_4[5]), .out_5(somador_1bit_6_out_5));
  somador_1bit somador_1bit_7 (
    .a(in_2[6]), .b(in_3[6]), .c_in(somador_1bit_6_out_5), .out_4(out_4[6]), .out_5(somador_1bit_7_out_5));
  somador_1bit somador_1bit_8 (.a(in_2[7]), .b(in_3[7]), .c_in(somador_1bit_7_out_5), .out_4(out_4[7]), .out_5(out_5));
endmodule

module memory_1bit (
  input  in_1,
  input  in_2,
  output out_3
);

  wire nand_1_out, nand_2_out, nand_4_out;

  nand nand_1 (nand_1_out, in_1, in_2);
  nand nand_2 (nand_2_out, in_2, nand_1_out);
  nand nand_3 (out_3, nand_1_out, nand_4_out);
  nand nand_4 (nand_4_out, out_3, nand_2_out);
endmodule

module registrador (
  input  [7:0] in_1,
  input  in_2,
  output [7:0] out_3
);

  memory_1bit memory_1bit_1 (.in_1(in_1[0]), .in_2(in_2), .out_3(out_3[0]));
  memory_1bit memory_1bit_2 (.in_1(in_1[1]), .in_2(in_2), .out_3(out_3[1]));
  memory_1bit memory_1bit_3 (.in_1(in_1[2]), .in_2(in_2), .out_3(out_3[2]));
  memory_1bit memory_1bit_4 (.in_1(in_1[3]), .in_2(in_2), .out_3(out_3[3]));
  memory_1bit memory_1bit_5 (.in_1(in_1[4]), .in_2(in_2), .out_3(out_3[4]));
  memory_1bit memory_1bit_6 (.in_1(in_1[5]), .in_2(in_2), .out_3(out_3[5]));
  memory_1bit memory_1bit_7 (.in_1(in_1[6]), .in_2(in_2), .out_3(out_3[6]));
  memory_1bit memory_1bit_8 (.in_1(in_1[7]), .in_2(in_2), .out_3(out_3[7]));
endmodule

module enable (
  input  [7:0] in_1,
  input  in_2,
  output [7:0] out_3
);

  assign out_3 = in_2 ? in_1 : 8'bz;  // Controlled_Buffer controlled_buffer_1
endmodule

module registradorsetenable (
  input  [7:0] in_1,
  input  in_2,
  input  in_3,
  output [7:0] out_4
);

  wire [7:0] registrador_1_out_3;

  registrador registrador_1 (.in_1(in_1), .in_2(in_2), .out_3(registrador_1_out_3));
  enable enable_1 (.in_1(registrador_1_out_3), .in_2(in_3), .out_3(out_4));
endmodule

module decoder_2x4 (
  input  in_1,
  input  in_2,
  output out_3,
  output out_4,
  output out_5,
  output out_6
);

  wire not_1_out, not_2_out;

  not not_1 (not_1_out, in_1);
  not not_2 (not_2_out, in_2);
  and and_1 (out_3, not_1_out, not_2_out);
  and and_2 (out_4, in_1, not_2_out);
  and and_3 (out_5, not_1_out, in_2);
  and and_4 (out_6, in_1, in_2);
endmodule

module memory_16bit (
  input  [7:0] in_1,
  input  we,
  input  oe,
  input  [7:0] in_4,
  output [7:0] out_5
);

  wire and_1_out, and_2_out, and_3_out, decoder_1_out0, decoder_2_out0;

  Decoder #(.select(4)) decoder_1 (
    .out0(decoder_1_out0), .sel(in_1[7:4]));  // open: out1, out2, out3, out4, out5, out6, out7, out8, out9, out10, out11, out12, out13, out14, out15, en
  Decoder #(.select(4)) decoder_2 (
    .out0(decoder_2_out0), .sel(in_1[3:0]));  // open: out1, out2, out3, out4, out5, out6, out7, out8, out9, out10, out11, out12, out13, out14, out15, en
  and and_1 (and_1_out, decoder_2_out0, decoder_1_out0);
  and and_2 (and_2_out, and_1_out, we);
  registradorsetenable registradorsetenable_1 (.in_1(in_4), .in_2(and_2_out), .in_3(and_3_out), .out_4(out_5));
  and and_3 (and_3_out, and_1_out, oe);
endmodule

module shift_right (
  input  in_1,
  input  [7:0] in_2,
  output [7:0] out_3,
  output out_4
);


  assign out_3 = {in_1, in_2[7:1]};
  assign out_4 = in_2[0];
endmodule

module ula (
  input  [2:0] in_1,
  input  [7:0] in_2,
  input  [7:0] in_3,
  output out_4,
  output [7:0] out_5,
  output a_maior_que_b,
  output a_igual_b,
  output out_8
);

  wire adder_1_cout, shift_right_1_out_4, shl_1_out_4;
  wire [7:0] adder_1_out, and_1_out, not_1_out, or_1_out, shift_right_1_out_3, shl_1_out_3, xnor_1_out;

  Comparator comparator_1 (.a(in_2), .b(in_3), .gt(a_maior_que_b), .eq(a_igual_b));  // open: lt
  Adder adder_1 (.a(in_2), .b(in_3), .out(adder_1_out), .cin(1'b0), .cout(adder_1_cout));
  shift_right shift_right_1 (.in_2(in_2), .in_1(1'b0), .out_4(shift_right_1_out_4), .out_3(shift_right_1_out_3));
  shl shl_1 (.in_2(in_2), .in_1(1'b0), .out_4(shl_1_out_4), .out_3(shl_1_out_3));
  assign not_1_out = ~in_2;  // NOT_Gate not_1, 8 bits wide
  assign and_1_out = in_2 & in_3;  // AND_Gate and_1, 8 bits wide
  assign or_1_out = in_2 | in_3;  // OR_Gate or_1, 8 bits wide
  assign xnor_1_out = ~(in_2 ^ in_3);  // XNOR_Gate xnor_1, 8 bits wide
  Multiplexer #(.select(3), .width(8)) multiplexer_1 (
    .in0(adder_1_out), .in1(shift_right_1_out_3), .in2(shl_1_out_3), .in3(not_1_out), .in4(and_1_out),
    .in5(or_1_out), .in6(xnor_1_out), .in7(in_2), .out(out_5), .sel(in_1));
  Multiplexer #(.select(3)) multiplexer_2 (
    .in0(adder_1_cout), .in1(shift_right_1_out_4), .in2(shl_1_out_4), .in3(1'b0), .in4(1'b0), .in5(1'b0),
    .in6(1'b0), .in7(1'b0), .out(out_4), .sel(in_1));
  nor nor_1 (out_8, out_5[0], out_5[1], out_5[2], out_5[3], out_5[4], out_5[5], out_5[6], out_5[7]);
endmodule

module shl (
  input  in_1,
  input  [7:0] in_2,
  output [7:0] out_3,
  output out_4
);


  assign out_3 = {in_2[6:0], in_1};
  assign out_4 = in_2[7];
endmodule
